// Logisim project tinycpu.circ as structural Verilog: 2 circuits, main circuit main
module main (
  input  in_1,
  input  DFF_D1,
  input  ADD_C1,
  input  DFF_D2,
  input  S,
  input  ADD_A1,
  input  in_7,
  input  in_8,
  input  ADD_B1,
  input  R,
  input  in_11,
  input  in_12,
  input  in_13,
  input  DFF_EN,
  input  D,
  input  EN,
  input  in_17,
  input  in_18,
  input  [7:0] in_19,
  input  in_20,
  input  in_21,
  input  in_22,
  input  [7:0] in_23,
  input  in_24,
  input  ram_we,
  input  MUX1_SEL,
  input  MUX_A,
  input  MUX_B,
  input  MUX_C,
  input  MUX_D,
  input  in_31,
  input  in_32,
  input  in_33,
  input  in_34,
  input  mux_a2,
  input  mux_b2,
  input  [7:0] in_37,
  input  in_38,
  input  mux_c2,
  input  mux_d2,
  input  [1:0] MUX_SEL,
  output [2:0] out_42,
  output [7:0] out_43,
  output [7:0] out_44,
  output [7:0] out_45,
  output [7:0] out_46
);

  wire and_1_out, and_2_out, and_3_out, and_4_out, and_5_out, and_6_out, and_7_out, and_8_out, and_9_out,
       and_10_out, and_11_out, and_12_out, and_13_out, and_14_out, and_15_out, and_16_out, and_17_out,
       and_18_out, and_19_out, and_20_out, and_21_out, and_22_out, and_23_out, and_24_out, and_25_out,
       and_26_out, and_27_out, and_28_out, and_29_out, clock_1_out, clock_2_out, decoder_1_out0,
       decoder_1_out1, DFF_clk_out, nor_3_out, nor_4_out, nor_5_out, nor_6_out, nor_7_out, nor_8_out,
       nor_9_out, nor_10_out, nor_11_out, not_1_out, not_2_out, not_3_out, not_4_out, not_5_out, not_6_out,
       not_7_out, not_8_out, not_9_out, not_10_out, not_11_out, not_12_out, or_1_out, or_2_out, or_3_out,
       or_4_out, or_5_out, or_6_out, or_7_out, or_8_out, or_9_out, or_10_out, or_11_out, or_12_out,
       or_13_out, SUM_x_out, SUM_y_out, undriven, xor_2_out, xor_3_out, xor_4_out;
  wire [3:0] REG_MAR;
  wire [7:0] multiplexer_1_out, RAM1, undriven_2, undriven_3;

  not not_1 (not_1_out, D);
  not not_2 (not_2_out, MUX1_SEL);
  not not_3 (not_3_out, MUX1_SEL);
  nor nor_1 (in_1, S, in_13);
  nor nor_2 (in_13, in_1, R);
  and and_1 (and_1_out, D, EN);
  and and_2 (and_2_out, in_17, not_2_out);
  and and_3 (and_3_out, in_21, MUX1_SEL);
  and and_4 (and_4_out, in_18, not_3_out);
  and and_5 (and_5_out, in_22, MUX1_SEL);
  and and_6 (and_6_out, not_1_out, EN);
  not not_4 (not_4_out, MUX_SEL[0]);
  nor nor_3 (nor_3_out, and_1_out, nor_4_out);
  nor nor_4 (nor_4_out, nor_3_out, and_6_out);
  or or_1 (or_1_out, and_2_out, and_3_out);
  or or_2 (or_2_out, and_4_out, and_5_out);
  not not_5 (not_5_out, MUX_SEL[0]);
  not not_6 (not_6_out, MUX_SEL[0]);
  not not_7 (not_7_out, MUX_SEL[0]);
  and and_7 (and_7_out, mux_a2, not_4_out);
  and and_8 (and_8_out, mux_b2, MUX_SEL[0]);
  and and_9 (and_9_out, mux_c2, not_7_out);
  and and_10 (and_10_out, mux_d2, MUX_SEL[0]);
  and and_11 (and_11_out, MUX_A, not_5_out);
  and and_12 (and_12_out, MUX_B, MUX_SEL[0]);
  and and_13 (and_13_out, MUX_C, not_6_out);
  and and_14 (and_14_out, MUX_D, MUX_SEL[0]);
  or or_3 (or_3_out, and_11_out, and_12_out);
  or or_4 (or_4_out, and_7_out, and_8_out);
  or or_5 (or_5_out, and_9_out, and_10_out);
  Clock DFF_clk (.out(DFF_clk_out));
  or or_6 (or_6_out, and_13_out, and_14_out);
  not not_8 (not_8_out, MUX_SEL[1]);
  and and_15 (and_15_out, DFF_clk_out, DFF_EN);
  not not_9 (not_9_out, MUX_SEL[1]);
  and and_16 (and_16_out, or_4_out, not_8_out);
  and and_17 (and_17_out, or_5_out, MUX_SEL[1]);
  and and_18 (and_18_out, or_3_out, not_9_out);
  and and_19 (and_19_out, or_6_out, MUX_SEL[1]);
  or or_7 (or_7_out, and_16_out, and_17_out);
  not not_10 (not_10_out, DFF_D2);
  Register register_1 (.D(in_19), .en(in_20), .clk(clock_1_out), .Q(out_43));  // open: clr
  Clock clock_1 (.out(clock_1_out));
  Register register_2 (.D(in_23), .en(in_24), .clk(clock_2_out), .Q(out_44));  // open: clr
  Clock clock_2 (.out(clock_2_out));
  or or_8 (or_8_out, and_18_out, and_19_out);
  not not_11 (not_11_out, DFF_D1);
  and and_20 (and_20_out, DFF_D2, and_15_out);
  and and_21 (and_21_out, DFF_D1, and_15_out);
  and and_22 (and_22_out, not_11_out, and_15_out);
  not not_12 (not_12_out, DFF_clk_out);
  and and_23 (and_23_out, not_10_out, and_15_out);
  Register #(.width(4)) mem_addr_register (.en(undriven), .Q(REG_MAR));  // open: D, clk, clr
  nor nor_5 (nor_5_out, and_21_out, nor_6_out);
  nor nor_6 (nor_6_out, nor_5_out, and_22_out);
  nor nor_7 (nor_7_out, and_20_out, nor_8_out);
  nor nor_8 (nor_8_out, nor_7_out, and_23_out);
  and and_24 (and_24_out, nor_5_out, not_12_out);
  and and_25 (and_25_out, nor_6_out, not_12_out);
  Decoder #(.select(4)) decoder_1 (
    .out0(decoder_1_out0), .out1(decoder_1_out1), .sel(REG_MAR), .en(ram_we));  // open: out2, out3, out4, out5, out6, out7, out8, out9, out10, out11, out12, out13, out14, out15
  or or_9 (or_9_out, in_31, in_32);
  or or_10 (or_10_out, in_33, in_34);
  assign out_45 = {{7{in_38}}, in_38};  // Bit_Extender bit_extender_1
  nor nor_9 (nor_9_out, and_24_out, nor_10_out);
  nor nor_10 (nor_10_out, nor_9_out, and_25_out);
  nor nor_11 (nor_11_out, or_9_out, or_10_out);
  Register register_3 (.D(undriven_2), .en(decoder_1_out0), .Q(RAM1));  // open: clk, clr
  Register register_4 (.en(decoder_1_out1));  // open: D, clk, Q, clr
  Register register_5 ();  // open: D, en, clk, Q, clr
  Register register_6 ();  // open: D, en, clk, Q, clr
  assign out_46 = in_37 ^ out_45;  // XOR_Gate xor_1, 8 bits wide
  Register register_7 (.D(undriven_3));  // open: en, clk, Q, clr
  Register register_8 ();  // open: D, en, clk, Q, clr
  Register register_9 ();  // open: D, en, clk, Q, clr
  Register register_10 ();  // open: D, en, clk, Q, clr
  xor xor_2 (xor_2_out, ADD_A1, ADD_B1);
  xor xor_3 (xor_3_out, in_7, in_11);
  xor xor_4 (xor_4_out, in_8, in_12);
  Register register_11 ();  // open: D, en, clk, Q, clr
  Register register_12 ();  // open: D, en, clk, Q, clr
  Register register_13 ();  // open: D, en, clk, Q, clr
  Register register_14 ();  // open: D, en, clk, Q, clr
  xor SUM_i (out_42[0], xor_2_out, ADD_C1);
  and SUM_y (SUM_y_out, xor_2_out, ADD_C1);
  and SUM_x (SUM_x_out, ADD_A1, ADD_B1);
  and and_26 (and_26_out, xor_3_out, or_11_out);
  and and_27 (and_27_out, in_7, in_11);
  and and_28 (and_28_out, xor_4_out, or_12_out);
  and and_29 (and_29_out, in_8, in_12);
  xor xor_5 (out_42[1], xor_3_out, or_11_out);
  xor xor_6 (out_42[2], xor_4_out, or_12_out);
  or or_11 (or_11_out, SUM_y_out, SUM_x_out);
  or or_12 (or_12_out, and_26_out, and_27_out);
  or or_13 (or_13_out, and_28_out, and_29_out);
  Register register_15 ();  // open: D, en, clk, Q, clr
  Register register_16 ();  // open: D, en, clk, Q, clr
  Register register_17 ();  // open: D, en, clk, Q, clr
  Register register_18 ();  // open: D, en, clk, Q, clr
  Multiplexer #(.select(4), .width(8)) multiplexer_1 (
    .in0(RAM1), .out(multiplexer_1_out), .sel(REG_MAR));  // open: in1, in2, in3, in4, in5, in6, in7, in8, in9, in10, in11, in12, in13, in14, in15

  // Other names for the same wires on the sheet: in_extended[7:0] = out_45; xor_out[7:0] = out_46
endmodule

module cpu (
  input  in_1,
  input  in_2,
  input  in_3,
  output [7:0] out_4,
  output [7:0] out_5,
  output [7:0] out_6,
  output [7:0] out_7,
  output [3:0] out_8,
  output [7:0] out_9,
  output [7:0] out_10,
  output [7:0] out_11,
  output [7:0] out_12,
  output [11:0] out_13,
  output [3:0] out_14,
  output [7:0] out_15,
  output [7:0] out_16
);

  wire A_WE, ALU_SUB, B_WE, C_WE, CLK, clock_1_out, INSTR_STEP_RESET, IS_ALU_ZERO, not_1_out, PC_WE;
  wire [3:0] PC_D, PC_NEXT, REG_PC;
  wire [7:0] INST_ADDR_EXT;
  wire [12:0] CONTROL_FLAGS;

  not not_1 (not_1_out, CONTROL_FLAGS[3]);
  Clock clock_1 (.out(clock_1_out));
  assign INST_ADDR_EXT = {{4{1'b0}}, out_12[3:0]};  // Bit_Extender bit_extender_1
  and and_1 (CLK, not_1_out, clock_1_out);
  or or_1 (INSTR_STEP_RESET, CONTROL_FLAGS[4], in_2, in_3);
  Register REG_A (.D(out_4), .en(A_WE), .clk(CLK), .Q(out_5), .clr(in_2));
  Register REG_B (.D(out_4), .en(B_WE), .clk(CLK), .Q(out_6), .clr(in_2));
  Register REG_C (.D(out_4), .en(C_WE), .clk(CLK), .Q(out_7), .clr(in_2));
  Register #(.width(4)) REG_MAR (.D(out_4[3:0]), .en(CONTROL_FLAGS[12]), .clk(CLK), .Q(out_8), .clr(in_2));
  Register REG_INST (.D(out_4), .en(CONTROL_FLAGS[8]), .clk(CLK), .Q(out_12), .clr(in_2));
  Register #(.width(4)) u_REG_PC (.D(PC_D), .en(PC_WE), .clk(CLK), .Q(REG_PC), .clr(in_2));
  Register #(.width(4)) register_1 (.D(out_14), .en(1'b1), .clk(CLK), .Q(out_13[7:4]), .clr(INSTR_STEP_RESET));
  ROM #(.addrWidth(12), .dataWidth(16)) rom_1 (
    .addr({out_12[7:4], out_13[7:0]}),
    .data({A_WE, B_WE, C_WE, CONTROL_FLAGS[12:3], ALU_SUB, CONTROL_FLAGS[1:0]}));
  Adder #(.width(4)) adder_1 (.a(REG_PC), .b(4'b0001), .out(PC_NEXT));  // open: cin, cout
  assign out_11 = {{4{1'b0}}, REG_PC};  // Bit_Extender bit_extender_2
  Adder #(.width(4)) adder_2 (.a(out_13[7:4]), .b(4'b0001), .out(out_14));  // open: cin, cout
  RAM #(.addrWidth(4), .asyncread("true"), .\type ("nonvolatile")) ram_1 (
    .addr(out_8), .we(CONTROL_FLAGS[11]), .oe(1'b1), .clk(CLK), .din(out_4), .dout(out_10));
  Multiplexer #(.select(3), .width(8)) multiplexer_1 (
    .in0(out_5), .in1(out_6), .in2(out_7), .in3(out_9), .in4(out_10), .in5(out_11), .in6(INST_ADDR_EXT),
    .out(out_4), .sel(CONTROL_FLAGS[7:5]));  // open: in7
  or or_2 (PC_WE, CONTROL_FLAGS[10], CONTROL_FLAGS[9]);
  assign out_16 = {{7{ALU_SUB}}, ALU_SUB};  // Bit_Extender bit_extender_3
  Multiplexer #(.select(2), .width(4)) multiplexer_2 (
    .in1(PC_NEXT), .in2(out_4[3:0]), .out(PC_D), .sel({CONTROL_FLAGS[9], CONTROL_FLAGS[10]}));  // open: in0, in3
  assign out_15 = out_6 ^ out_16;  // XOR_Gate xor_1, 8 bits wide
  Adder adder_3 (.a(out_5), .b(out_15), .out(out_9), .cin(ALU_SUB));  // open: cout
  nor nor_1 (IS_ALU_ZERO, out_9[0], out_9[1], out_9[2], out_9[3], out_9[4], out_9[5], out_9[6], out_9[7]);
  assign out_13[3:0] = {{3{1'b0}}, IS_ALU_ZERO};  // Bit_Extender bit_extender_4

  assign out_13[11:8] = out_12[7:4];

  // Other names for the same wires on the sheet: ALU_OUT[7:0] = out_9; ALU_SUB_EXT[7:0] = out_16;
  //   CONTROL_FLAGS (some bits) = {A_WE, B_WE, C_WE, ALU_SUB}; HLT = CONTROL_FLAGS[3];
  //   INSTR_STEP_RESET_CTRL = CONTROL_FLAGS[4]; INST_WE = CONTROL_FLAGS[8]; RAM_WE = CONTROL_FLAGS[11];
  //   MAR_WE = CONTROL_FLAGS[12]; CPU_RST = in_2; INSTR_STEP_NEXT[3:0] = out_14; INSTR_STEP_RESET_BTN = in_3;
  //   PC_CLR = in_1; PC_INC = CONTROL_FLAGS[10]; PC_MUX_SEL[1:0] = {CONTROL_FLAGS[9], CONTROL_FLAGS[10]};
  //   PC_JMP = CONTROL_FLAGS[9]; REG_A[7:0] = out_5; REG_B[7:0] = out_6; REG_B_WSUB[7:0] = out_15; REG_C[7:0] = out_7;
  //   INST_ADDR[3:0] = out_12[3:0]; REG_INST[7:0] = out_12; REG_MAR[3:0] = out_8; REG_PC_EXT[7:0] = out_11;
  //   REG_RAM[7:0] = out_10; REG_SEL[2:0] = CONTROL_FLAGS[7:5]; ALU_COND_FLAGS[3:0] = out_13[3:0];
  //   ROM_LOOKUP[11:0] = {out_12[7:4], out_13[7:0]}; INSTR_LOOKUP[7:0] = {out_12[7:4], out_13[7:4]};
  //   INSTR_STEP[3:0] = out_13[7:4]; INST_OPCODE[3:0] = out_12[7:4]; BUS_4_LSB[3:0] = out_4[3:0];
  //   THE_BUS[7:0] = out_4; BUS_4_MSB[3:0] = out_4[7:4]

  // Notes on the sheet:
  //   a = 0, b = 1, c = 2, alu = 3, ram = 4, pc = 5, inst=6
  //   contents of rom_1 (hex, n*v repeats v):
  //   16*10a0 16*580 16*10 208*0 16*10a0 16*580 16*10c0 16*8080 16*10 176*0 16*10a0 16*580 16*10c0 16*4080
  //   16*8060 16*10 160*0 16*10a0 16*580 16*10c0 16*4080 16*8064 16*10 160*0 16*10a0 16*580 16*10c0 16*800
  //   16*10 176*0 16*10a0 16*580 16*80c0 16*10 192*0 16*10a0 16*580 16*2c0 16*10 192*0 16*10a0 16*580 10
  //   2c0 10 2c0 10 2c0 10 2c0 10 2c0 10 2c0 10 2c0 10 2c0 16*10 192*0 16*10a0 16*580 224*0 16*10a0 16*580
  //   224*0 16*10a0 16*580 224*0 16*10a0 16*580 224*0 16*10a0 16*580 224*0 16*10a0 16*580 224*0 16*10a0
  //   16*580 224*0 16*10a0 16*580 16*8
endmodule
